# Fritzing sketch ChamberHeater_Sketch (saved by Fritzing 1.0.2b)
breadboards: 1

parts:
  WeMos_D1_Mini1 = WeMos D1 Mini
  DS1 = DS18B20 1-Wire Temperature Sensor [part_number=DS18B20]
  DHT1 = DHT22 Humidity and Temperature Sensor
  R1 = Resistor [tolerance=±5% power=0.25W resistance=9.1k package=THT]
  R2 = Resistor [tolerance=±5% power=0.25W resistance=4.7k package=THT]
  LCD1 = TFT 1.8 inch 160x128 w SD

nets:
  N1: WeMos_D1_Mini1.3V3, LCD1.pin_8
  VDD: WeMos_D1_Mini1.5V, DS1.VDD, DHT1.VDD, R1.Pin_1, R2.Pin_1, LCD1.pin_1
  N2: WeMos_D1_Mini1.D0, LCD1.pin_5
  N3: WeMos_D1_Mini1.D1, DHT1.DATA, R1.Pin_0
  N4: WeMos_D1_Mini1.D2, DS1.DQ, R2.Pin_0
  N5: WeMos_D1_Mini1.D3, LCD1.pin4
  N6: WeMos_D1_Mini1.D4, LCD1.pin3
  N7: WeMos_D1_Mini1.D5, LCD1.pin_7
  N8: WeMos_D1_Mini1.D7, LCD1.pin_6
  N9: WeMos_D1_Mini1.G, DS1.GND, DHT1.NULL, LCD1.pin2

custom parts:
  TFT 1.8 inch 160x128 w SD: This is a generic 1.8 tft spi lcd display available on ebay and others. The 1.8" display has 128x160 color pixels.
